// Logisim project LAB1.circ as structural Verilog: 11 circuits, main circuit lab1.1
module lab1_1 (
  input  A,
  input  B,
  output S,
  output C
);

  xor xor_1 (S, A, B);
  and and_1 (C, A, B);

  // Notes on the sheet:
  //   一位二进制半加器
endmodule

module lab1_2 (
  input  A,
  input  B,
  input  Ci,
  output S,
  output Co
);

  wire and_1_out, and_2_out, xor_1_out;

  xor xor_1 (xor_1_out, A, B);
  and and_1 (and_1_out, Ci, xor_1_out);
  and and_2 (and_2_out, A, B);
  xor xor_2 (S, xor_1_out, Ci);
  or or_1 (Co, and_1_out, and_2_out);

  // Notes on the sheet:
  //   B: pull=up
  //   一位二进制全加器
endmodule

module lab1_3 (
  input  A3,
  input  B3,
  input  A2,
  input  B2,
  input  A1,
  input  B1,
  input  A0,
  input  B0,
  input  Co,
  output S3,
  output C4,
  output S2,
  output S1,
  output S0
);

  lab1_2 lab1_2_1 (.B(B3), .Ci(S2), .S(S3), .Co(C4), .A(A3));
  lab1_2 lab1_2_2 (.B(B2), .Ci(S1), .S(S2), .Co(S2), .A(A2));
  lab1_2 lab1_2_3 (.B(B1), .Ci(S0), .S(S1), .Co(S1), .A(A1));
  lab1_2 lab1_2_4 (.B(B0), .Ci(Co), .S(S0), .Co(S0), .A(A0));

  // Notes on the sheet:
  //   串行进位四位二进制并行加法器
endmodule

module lab1_4 (
  input  in_1,
  input  in_2,
  input  in_3,
  input  in_4,
  input  in_5,
  input  in_6,
  input  in_7,
  input  in_8,
  input  in_9,
  output out_10,
  output out_11,
  output out_12,
  output out_13,
  output out_14
);

  lab1_5 lab1_5_1 (
    .A0(in_5), .B0(in_9), .Co(in_1), .A1(in_4), .B1(in_8), .A2(in_3), .B2(in_7), .A3(in_2), .B3(in_6),
    .S0(out_13), .S1(out_12), .S2(out_11), .S3(out_10), .C4(out_14));
endmodule

module lab1_5 (
  input  A0,
  input  B0,
  input  Co,
  input  A1,
  input  B1,
  input  A2,
  input  B2,
  input  A3,
  input  B3,
  output S0,
  output S1,
  output S2,
  output S3,
  output C4
);

  wire lab1_2_2_co, lab1_2_3_co, lab1_2_4_co, lab1_2_6_co, lab1_2_7_co, lab1_2_9_co;

  lab1_2 lab1_2_1 (.B(B0), .Ci(Co), .S(S0), .A(A0));  // open: Co
  lab1_2 lab1_2_2 (.B(B0), .Ci(Co), .Co(lab1_2_2_co), .A(A0));  // open: S
  lab1_2 lab1_2_3 (.B(B0), .Ci(Co), .Co(lab1_2_3_co), .A(A0));  // open: S
  lab1_2 lab1_2_4 (.B(B0), .Ci(Co), .Co(lab1_2_4_co), .A(A0));  // open: S
  lab1_2 lab1_2_5 (.B(B1), .Ci(lab1_2_2_co), .S(S1), .A(A1));  // open: Co
  lab1_2 lab1_2_6 (.B(B1), .Ci(lab1_2_3_co), .Co(lab1_2_6_co), .A(A1));  // open: S
  lab1_2 lab1_2_7 (.B(B1), .Ci(lab1_2_4_co), .Co(lab1_2_7_co), .A(A1));  // open: S
  lab1_2 lab1_2_8 (.B(B2), .Ci(lab1_2_6_co), .S(S2), .A(A2));  // open: Co
  lab1_2 lab1_2_9 (.B(B2), .Ci(lab1_2_7_co), .Co(lab1_2_9_co), .A(A2));  // open: S
  lab1_2 lab1_2_10 (.B(B3), .Ci(lab1_2_9_co), .S(S3), .Co(C4), .A(A3));

  // Notes on the sheet:
  //   四位二进制并行加法器
endmodule

module LAB2_1 (
  input  in_1,
  input  cpu,
  input  cpd,
  output out_4,
  output out_5,
  output out_6,
  output out_7
);

  wire and_1_out, and_2_out, and_3_out, not_1_out, not_2_out, or_1_out, xor_1_out, xor_2_out, xor_3_out,
       xor_4_out, xor_5_out, xor_6_out;

  or or_1 (or_1_out, cpd, cpu);
  not not_1 (not_1_out, cpu);
  and and_1 (and_1_out, not_1_out, cpd);
  xor xor_1 (xor_1_out, and_2_out, out_4);
  D_Flip_Flop #(.trigger("falling")) d_ff_1 (
    .clk(or_1_out), .D(xor_1_out), .Q(out_4), .en(1'b1), .reset(in_1));  // open: Qn, preset
  and and_2 (and_2_out, xor_3_out, and_3_out);
  D_Flip_Flop #(.trigger("falling")) d_ff_2 (
    .clk(or_1_out), .D(xor_2_out), .Q(out_5), .en(1'b1), .reset(in_1));  // open: Qn, preset
  xor xor_2 (xor_2_out, out_5, and_3_out);
  and and_3 (and_3_out, xor_6_out, xor_5_out);
  xor xor_3 (xor_3_out, and_1_out, out_5);
  xor xor_4 (xor_4_out, xor_6_out, out_6);
  xor xor_5 (xor_5_out, and_1_out, out_6);
  D_Flip_Flop #(.trigger("falling")) d_ff_3 (
    .clk(or_1_out), .D(xor_4_out), .Q(out_6), .en(1'b1), .reset(in_1));  // open: Qn, preset
  xor xor_6 (xor_6_out, and_1_out, out_7);
  D_Flip_Flop #(.trigger("falling")) d_ff_4 (
    .clk(or_1_out), .D(not_2_out), .Q(out_7), .en(1'b1), .reset(in_1));  // open: Qn, preset
  not not_2 (not_2_out, out_7);

  // Notes on the sheet:
  //   四位二进制可逆计数器
endmodule

module LAB2_2 (
  input  in_1,
  input  in_2,
  input  in_3,
  input  in_4,
  output out_5,
  output out_6,
  output out_7,
  output out_8,
  output out_9,
  output out_10,
  output out_11,
  output out_12
);

  wire and_1_out, or_1_out;

  or or_1 (or_1_out, in_2, in_3);
  lab1_5 lab1_5_1 (
    .A0(in_4), .B0(out_5), .Co(out_5), .A1(in_3), .B1(and_1_out), .A2(in_2), .B2(and_1_out), .A3(in_1),
    .B3(out_5), .S0(out_12), .S1(out_11), .S2(out_10), .S3(out_9), .C4(out_8));
  and and_1 (and_1_out, or_1_out, in_1);
  not not_1 (out_5, 1'b1);

  assign out_6 = out_5;
  assign out_7 = out_5;
endmodule

module LAB2_3 (
  input  in_1,
  input  in_2,
  input  in_3,
  input  in_4,
  output out_5,
  output out_6,
  output out_7,
  output out_8,
  output out_9,
  output out_10,
  output out_11
);

  wire and_1_out, and_2_out, and_3_out, and_4_out, and_5_out, and_6_out, and_7_out, and_8_out, and_9_out,
       not_4_out, not_6_out, not_7_out, not_8_out, or_1_out, or_2_out, or_3_out, or_5_out, or_6_out;

  and and_1 (and_1_out, not_4_out, not_6_out, not_7_out, in_4);
  and and_2 (and_2_out, not_4_out, in_2, not_7_out, not_8_out);
  and and_3 (and_3_out, not_4_out, in_2, not_7_out, in_4);
  not not_1 (out_5, or_1_out);
  not not_2 (out_6, or_2_out);
  or or_1 (or_1_out, and_1_out, and_2_out);
  or or_2 (or_2_out, and_3_out, and_4_out);
  and and_4 (and_4_out, not_4_out, in_2, in_3, not_8_out);
  not not_3 (out_7, and_5_out);
  and and_5 (and_5_out, not_4_out, not_6_out, in_3, not_8_out);
  not not_4 (not_4_out, in_1);
  not not_5 (out_8, or_3_out);
  or or_3 (or_3_out, and_1_out, and_2_out, and_6_out);
  and and_6 (and_6_out, not_4_out, in_2, in_3, in_4);
  not not_6 (not_6_out, in_2);
  not not_7 (not_7_out, in_3);
  or or_4 (out_9, and_9_out, and_4_out, and_5_out, and_7_out);
  and and_7 (and_7_out, in_1, not_6_out, not_7_out, not_8_out);
  not not_8 (not_8_out, in_4);
  not not_9 (out_10, or_5_out);
  or or_5 (or_5_out, and_1_out, and_5_out, and_6_out, and_8_out);
  and and_8 (and_8_out, not_4_out, not_6_out, in_3, in_4);
  not not_10 (out_11, or_6_out);
  or or_6 (or_6_out, and_1_out, and_6_out, and_9_out);
  and and_9 (and_9_out, not_8_out, not_7_out, not_6_out, not_4_out);

  // Notes on the sheet:
  //   7段译码器
endmodule

module LAB2_4 (
  input  in_1,
  input  in_2,
  input  in_3,
  input  in_4
);

  wire lab2_2_1_out_5, lab2_2_1_out_6, lab2_2_1_out_7, lab2_2_1_out_8, lab2_2_1_out_9, lab2_2_1_out_10,
       lab2_2_1_out_11, lab2_2_1_out_12, lab2_3_1_out_5, lab2_3_1_out_6, lab2_3_1_out_7, lab2_3_1_out_8,
       lab2_3_1_out_9, lab2_3_1_out_10, lab2_3_1_out_11, lab2_3_2_out_5, lab2_3_2_out_6, lab2_3_2_out_7,
       lab2_3_2_out_8, lab2_3_2_out_9, lab2_3_2_out_10, lab2_3_2_out_11;

  _7_Segment_Display u_7_segment_display_1 (
    .g(lab2_3_1_out_11), .f(lab2_3_1_out_10), .a(lab2_3_1_out_5), .b(lab2_3_1_out_6), .e(lab2_3_1_out_9),
    .d(lab2_3_1_out_8), .c(lab2_3_1_out_7));  // open: dp
  LAB2_3 lab2_3_1 (
    .out_5(lab2_3_1_out_5), .out_6(lab2_3_1_out_6), .out_7(lab2_3_1_out_7), .out_8(lab2_3_1_out_8),
    .out_9(lab2_3_1_out_9), .out_10(lab2_3_1_out_10), .out_11(lab2_3_1_out_11), .in_1(lab2_2_1_out_5),
    .in_2(lab2_2_1_out_6), .in_3(lab2_2_1_out_7), .in_4(lab2_2_1_out_8));
  _7_Segment_Display u_7_segment_display_2 (
    .g(lab2_3_2_out_11), .f(lab2_3_2_out_10), .a(lab2_3_2_out_5), .b(lab2_3_2_out_6), .e(lab2_3_2_out_9),
    .d(lab2_3_2_out_8), .c(lab2_3_2_out_7));  // open: dp
  LAB2_2 lab2_2_1 (
    .out_5(lab2_2_1_out_5), .out_6(lab2_2_1_out_6), .out_7(lab2_2_1_out_7), .out_8(lab2_2_1_out_8),
    .out_9(lab2_2_1_out_9), .out_10(lab2_2_1_out_10), .out_11(lab2_2_1_out_11), .out_12(lab2_2_1_out_12),
    .in_1(in_1), .in_2(in_2), .in_3(in_3), .in_4(in_4));
  LAB2_3 lab2_3_2 (
    .out_5(lab2_3_2_out_5), .out_6(lab2_3_2_out_6), .out_7(lab2_3_2_out_7), .out_8(lab2_3_2_out_8),
    .out_9(lab2_3_2_out_9), .out_10(lab2_3_2_out_10), .out_11(lab2_3_2_out_11), .in_1(lab2_2_1_out_9),
    .in_2(lab2_2_1_out_10), .in_3(lab2_2_1_out_11), .in_4(lab2_2_1_out_12));
endmodule

module LAB2_5 (
  input  in_1,
  input  in_2,
  input  in_3,
  output out_4,
  output out_5,
  output out_6,
  output out_7,
  output out_8,
  output out_9,
  output out_10,
  output out_11,
  output out_12,
  output out_13,
  output out_14,
  output out_15,
  output out_16,
  output out_17,
  output out_18
);

  wire and_2_out, and_3_out, lab2_1_1_out_4, lab2_1_1_out_5, lab2_1_1_out_6, lab2_1_1_out_7, lab2_2_1_out_5,
       lab2_2_1_out_6, lab2_2_1_out_7, lab2_2_1_out_8, lab2_2_1_out_9, lab2_2_1_out_10, lab2_2_1_out_11,
       lab2_2_1_out_12, not_1_out, or_1_out;

  not not_1 (not_1_out, out_18);
  and and_1 (out_18, lab2_1_1_out_4, lab2_1_1_out_5, lab2_1_1_out_6, lab2_1_1_out_7);
  or or_1 (or_1_out, lab2_1_1_out_4, lab2_1_1_out_5, lab2_1_1_out_6, lab2_1_1_out_7);
  and and_2 (and_2_out, not_1_out, in_1);
  and and_3 (and_3_out, in_3, or_1_out);
  LAB2_3 lab2_3_1 (
    .out_5(out_4), .out_6(out_5), .out_7(out_6), .out_8(out_7), .out_9(out_8), .out_10(out_9),
    .out_11(out_10), .in_1(lab2_2_1_out_5), .in_2(lab2_2_1_out_6), .in_3(lab2_2_1_out_7),
    .in_4(lab2_2_1_out_8));
  LAB2_2 lab2_2_1 (
    .out_5(lab2_2_1_out_5), .out_6(lab2_2_1_out_6), .out_7(lab2_2_1_out_7), .out_8(lab2_2_1_out_8),
    .out_9(lab2_2_1_out_9), .out_10(lab2_2_1_out_10), .out_11(lab2_2_1_out_11), .out_12(lab2_2_1_out_12),
    .in_1(lab2_1_1_out_4), .in_2(lab2_1_1_out_5), .in_3(lab2_1_1_out_6), .in_4(lab2_1_1_out_7));
  LAB2_1 lab2_1_1 (
    .in_1(in_2), .cpu(and_2_out), .cpd(and_3_out), .out_7(lab2_1_1_out_7), .out_4(lab2_1_1_out_4),
    .out_5(lab2_1_1_out_5), .out_6(lab2_1_1_out_6));
  LAB2_3 lab2_3_2 (
    .out_5(out_11), .out_6(out_12), .out_7(out_13), .out_8(out_14), .out_9(out_15), .out_10(out_16),
    .out_11(out_17), .in_1(lab2_2_1_out_9), .in_2(lab2_2_1_out_10), .in_3(lab2_2_1_out_11),
    .in_4(lab2_2_1_out_12));
endmodule

module LAB2_6 (
  input  in_1,
  input  in_2,
  input  in_3
);

  wire lab2_5_1_out_4, lab2_5_1_out_5, lab2_5_1_out_6, lab2_5_1_out_7, lab2_5_1_out_8, lab2_5_1_out_9,
       lab2_5_1_out_10, lab2_5_1_out_11, lab2_5_1_out_12, lab2_5_1_out_13, lab2_5_1_out_14, lab2_5_1_out_15,
       lab2_5_1_out_16, lab2_5_1_out_17, lab2_5_1_out_18;

  _7_Segment_Display u_7_segment_display_1 (
    .g(lab2_5_1_out_10), .f(lab2_5_1_out_9), .a(lab2_5_1_out_4), .b(lab2_5_1_out_5), .e(lab2_5_1_out_8),
    .d(lab2_5_1_out_7), .c(lab2_5_1_out_6));  // open: dp
  _7_Segment_Display u_7_segment_display_2 (
    .g(lab2_5_1_out_17), .f(lab2_5_1_out_16), .a(lab2_5_1_out_11), .b(lab2_5_1_out_12), .e(lab2_5_1_out_15),
    .d(lab2_5_1_out_14), .c(lab2_5_1_out_13));  // open: dp
  LAB2_5 lab2_5_1 (
    .in_1(in_1), .in_2(in_2), .in_3(in_3), .out_4(lab2_5_1_out_4), .out_5(lab2_5_1_out_5),
    .out_7(lab2_5_1_out_7), .out_9(lab2_5_1_out_9), .out_14(lab2_5_1_out_14), .out_15(lab2_5_1_out_15),
    .out_16(lab2_5_1_out_16), .out_17(lab2_5_1_out_17), .out_6(lab2_5_1_out_6), .out_8(lab2_5_1_out_8),
    .out_10(lab2_5_1_out_10), .out_11(lab2_5_1_out_11), .out_12(lab2_5_1_out_12), .out_13(lab2_5_1_out_13),
    .out_18(lab2_5_1_out_18));
  LED led_1 (.in(lab2_5_1_out_18));
endmodule
